# Fritzing sketch dc-motor-control (saved by Fritzing 0.9.10b)

parts:
  AC_Power_Source = AC Power [voltage=220V frequency=60]
  12v-to-5v_Step-Down_Converter = RioRand LM2596
  12vDC_Power_Supply = HLK-PM12 [part_number=HLK-PM12]
  Motor_Driver = BTS7960
  MCU = DOIT Esp32 DevKit v1 (30 pins long, 11 pins width) [part_number=ESP32-PIN30]
  12v_DC_Motor = DC Motor [voltage_(max)=12V voltage_(min)=5V]

nets:
  N1: AC_Power_Source.V+, 12vDC_Power_Supply.AC_1
  N2: AC_Power_Source.V-, 12vDC_Power_Supply.AC_2
  N3: 12v-to-5v_Step-Down_Converter.Pin_1, 12vDC_Power_Supply.+Vo, Motor_Driver.pin11
  N4: 12v-to-5v_Step-Down_Converter.Pin_2, 12vDC_Power_Supply.-Vo, Motor_Driver.pin12
  N5: 12v-to-5v_Step-Down_Converter.Pin_3, Motor_Driver.pin7, MCU.VIN
  N6: 12v-to-5v_Step-Down_Converter.Pin_4, Motor_Driver.pin8, MCU.GND
  N7: Motor_Driver.pin1, MCU.D13
  N8: Motor_Driver.pin2, MCU.D12
  N9: Motor_Driver.pin3, MCU.D14
  N10: Motor_Driver.pin4, MCU.D27
  N11: Motor_Driver.pin9, 12v_DC_Motor.pin_1
  N12: Motor_Driver.pin10, 12v_DC_Motor.pin_2

custom parts:
  BTS7960: BTS7960 43A Peak Power H-Bridge PWM Motor Driver
  DOIT Esp32 DevKit v1 (30 pins long, 11 pins width): The DOIT Esp32 DevKit v1 is one of the development board created by DOIT to evaluate the ESP-WROOM-32 module. It is based on the ESP32 microcontroller that boasts Wifi, Bluetooth, Ethernet and Low Power support all in a single chip. (vanepp) made breadboard work, adjusted pin numbering and labels and reduced size of schematic and cleaned up pcb. This chip is 30pins long (2 x15) and 11 pins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
